// Logisim project TETRIS.circ as structural Verilog: 1 circuit, main circuit main
module main (
  input  in_1,
  input  in_2,
  input  in_3
);

  wire button_1_out, keyboard_1_avail, tetris_1_out_23;
  wire [6:0] keyboard_1_data;
  wire [7:0] tetris_1_out_7, tetris_1_out_8, tetris_1_out_9, tetris_1_out_10, tetris_1_out_11,
       tetris_1_out_12, tetris_1_out_13, tetris_1_out_14, tetris_1_out_15, tetris_1_out_16, tetris_1_out_17,
       tetris_1_out_18, tetris_1_out_19, tetris_1_out_20, tetris_1_out_21, tetris_1_out_22;

  DotMatrix #(.inputtype("row"), .matrixcols(8), .matrixrows(16)) dotmatrix_1 (
    .row0(tetris_1_out_7), .row1(tetris_1_out_8), .row2(tetris_1_out_9), .row3(tetris_1_out_10),
    .row4(tetris_1_out_11), .row5(tetris_1_out_12), .row6(tetris_1_out_13), .row7(tetris_1_out_14),
    .row8(tetris_1_out_15), .row9(tetris_1_out_16), .row10(tetris_1_out_17), .row11(tetris_1_out_18),
    .row12(tetris_1_out_19), .row13(tetris_1_out_20), .row14(tetris_1_out_21), .row15(tetris_1_out_22));
  Tetris tetris_1 (
    .out_23(tetris_1_out_23), .in_5(keyboard_1_avail), .in_6(keyboard_1_data), .in_4(button_1_out),
    .out_7(tetris_1_out_7), .out_8(tetris_1_out_8), .out_9(tetris_1_out_9), .out_10(tetris_1_out_10),
    .out_11(tetris_1_out_11), .out_12(tetris_1_out_12), .out_13(tetris_1_out_13), .out_14(tetris_1_out_14),
    .out_15(tetris_1_out_15), .out_16(tetris_1_out_16), .out_17(tetris_1_out_17), .out_18(tetris_1_out_18),
    .out_19(tetris_1_out_19), .out_20(tetris_1_out_20), .out_21(tetris_1_out_21), .out_22(tetris_1_out_22),
    .Easy(in_2), .Medium(in_3), .Hard(in_1));
  Button button_1 (.out(button_1_out));
  Keyboard keyboard_1 (.clr(tetris_1_out_23), .avail(keyboard_1_avail), .data(keyboard_1_data));  // open: clk, re

  // Notes on the sheet:
  //   1. Poziom trudności
  //   3. Start
  //   2. Taktowanie zegarowe włączone
  //   Lewo Prawo - A D
  //   Obrót Lewo Prawo - Q E
endmodule
